// Logisim project muxrisccore.circ as structural Verilog: 2 circuits, main circuit core
module core (
);

  wire alu_1_we, and_1_out, and_2_out, and_3_out, and_4_out, bitselector_1_out, bitselector_2_out,
       bitselector_7_out, bitselector_8_out, bitselector_9_out, bitselector_13_out, bitselector_14_out,
       bitselector_15_out, bitselector_16_out, bitselector_17_out, bitselector_18_out, bitselector_19_out,
       bitselector_20_out, bitselector_21_out, bitselector_22_out, bitselector_23_out, bitselector_24_out,
       bitselector_25_out, bitselector_26_out, bitselector_27_out, bitselector_28_out, bitselector_29_out,
       bitselector_30_out, clock_1_out, clock_2_out, clock_3_out, clock_4_out, clock_5_out, clock_6_out,
       comparator_1_eq, comparator_2_eq, comparator_3_eq, comparator_4_eq, comparator_5_eq, comparator_5_gt,
       comparator_5_lt, comparator_6_eq, multiplexer_1_out, not_1_out, not_2_out, not_3_out, or_1_out,
       regX_p2, regX_p14, regX_p15, regX_p16, regX_p17, regX_p18, regX_p19, regX_p20, regY_p11, regY_p12,
       regY_p13, regY_p14, regY_p15, regY_p16, regY_p17, regZ_p11, regZ_p12, regZ_p13, regZ_p14, regZ_p15,
       regZ_p16, regZ_p17;
  wire [3:0] bitselector_11_out, bitselector_12_out;
  wire [7:0] bitselector_10_out;
  wire [15:0] bitselector_3_out, bitselector_4_out, bitselector_5_out, bitselector_6_out;
  wire [23:0] bitselector_31_out, bitselector_32_out, counter_2_q;
  wire [31:0] counter_1_q;
  wire [63:0] alu_1_outx, ram1_p10, register_1_q, regX_p12, regX_p13, regY_p10, regZ_p10, undriven;

  BitSelector bitselector_1 (.in(bitselector_10_out), .out(bitselector_1_out), .sel(3'b111));
  BitSelector bitselector_2 (.in(bitselector_10_out), .out(bitselector_2_out), .sel(3'b110));
  BitSelector #(.group(16), .width(64)) bitselector_3 (.in(register_1_q), .out(bitselector_3_out), .sel(2'b11));
  BitSelector #(.group(16), .width(64)) bitselector_4 (.in(register_1_q), .out(bitselector_4_out), .sel(2'b10));
  BitSelector #(.group(16), .width(64)) bitselector_5 (.in(register_1_q), .out(bitselector_5_out), .sel(2'b01));
  BitSelector #(.group(16), .width(64)) bitselector_6 (.in(register_1_q), .out(bitselector_6_out), .sel(2'b00));
  Register #(.trigger("falling"), .width(64)) register_1 (
    .D(ram1_p10), .en(1'b1), .clk(clock_1_out), .Q(register_1_q));  // open: clr
  Clock clock_1 (.out(clock_1_out));
  BitSelector bitselector_7 (.in(bitselector_10_out), .out(bitselector_7_out), .sel(3'b101));
  BitSelector bitselector_8 (.in(bitselector_10_out), .out(bitselector_8_out), .sel(3'b100));
  BitSelector bitselector_9 (.in(bitselector_10_out), .out(bitselector_9_out), .sel(3'b011));
  BitSelector #(.group(8), .width(16)) bitselector_10 (.in(bitselector_6_out), .out(bitselector_10_out), .sel(1'b1));
  BitSelector #(.group(4), .width(16)) bitselector_11 (.in(bitselector_6_out), .out(bitselector_11_out), .sel(2'b01));
  BitSelector #(.group(4), .width(16)) bitselector_12 (.in(bitselector_6_out), .out(bitselector_12_out), .sel(2'b00));
  BitSelector bitselector_13 (.in(bitselector_10_out), .out(bitselector_13_out), .sel(3'b010));
  BitSelector bitselector_14 (.in(bitselector_10_out), .out(bitselector_14_out), .sel(3'b001));
  Clock clock_2 (.out(clock_2_out));
  BitSelector #(.width(4)) bitselector_15 (.in(bitselector_11_out), .out(bitselector_15_out), .sel(2'b00));
  BitSelector #(.width(4)) bitselector_16 (.in(bitselector_11_out), .out(bitselector_16_out), .sel(2'b00));
  // RAM #(.addrWidth(16), .dataWidth(64), .enables("line"), .line("octo"), .misaligned("true")) regX: pin names not known; wires that end beside it: bitselector_3_out, regX_p2, regX_p2, bitselector_14_out, bitselector_13_out, bitselector_9_out, bitselector_8_out, bitselector_7_out, bitselector_2_out, bitselector_1_out, clock_2_out, regX_p12, regX_p13, regX_p14, regX_p15, regX_p16, regX_p17, regX_p18, regX_p19, regX_p20
  Comparator #(.mode("unsigned"), .width(4)) comparator_1 (
    .a(bitselector_12_out), .b(4'b0000), .eq(comparator_1_eq));  // open: gt, lt
  Counter #(.max('hffffffff), .trigger("falling"), .width(32)) counter_1 (
    .load(or_1_out), .D({32{1'b0}}), .count(comparator_1_eq), .Q(counter_1_q), .clk(clock_3_out));  // open: carry, up, clr
  Clock clock_3 (.out(clock_3_out));
  Comparator #(.mode("unsigned"), .width(4)) comparator_2 (
    .a(bitselector_12_out), .b(4'b0001), .eq(comparator_2_eq));  // open: gt, lt
  Comparator #(.mode("unsigned"), .width(4)) comparator_3 (
    .a(bitselector_12_out), .b(4'b0010), .eq(comparator_3_eq));  // open: gt, lt
  Comparator #(.mode("unsigned"), .width(4)) comparator_4 (
    .a(bitselector_12_out), .b(4'b0011), .eq(comparator_4_eq));  // open: gt, lt
  and and_1 (and_1_out, comparator_4_eq, bitselector_16_out);
  not not_1 (not_1_out, bitselector_16_out);
  Comparator #(.mode("unsigned"), .width(32)) comparator_5 (
    .a(counter_1_q), .b({bitselector_4_out, bitselector_5_out}), .gt(comparator_5_gt), .eq(comparator_5_eq),
    .lt(comparator_5_lt));
  and and_2 (and_2_out, not_1_out, comparator_4_eq);
  or or_1 (or_1_out, comparator_5_gt, comparator_5_eq);
  and and_3 (and_3_out, comparator_5_lt, comparator_1_eq);
  Comparator #(.mode("unsigned"), .width(64)) comparator_6 (
    .a(regY_p10), .b({64{1'b0}}), .eq(comparator_6_eq));  // open: gt, lt
  not not_2 (not_2_out, comparator_6_eq);
  alu alu_1 (
    .argY(regY_p10), .argZ(regZ_p10), .op(bitselector_12_out), .\var (bitselector_11_out), .outX(alu_1_outx),
    .we(alu_1_we));
  and and_4 (and_4_out, not_2_out, comparator_2_eq);
  BitSelector bitselector_17 (.in(bitselector_10_out), .out(bitselector_17_out), .sel(3'b111));
  BitSelector bitselector_18 (.in(bitselector_10_out), .out(bitselector_18_out), .sel(3'b110));
  Multiplexer multiplexer_1 (.in0(and_4_out), .in1(comparator_2_eq), .out(multiplexer_1_out), .sel(bitselector_15_out));
  BitSelector bitselector_19 (.in(bitselector_10_out), .out(bitselector_19_out), .sel(3'b100));
  BitSelector bitselector_20 (.in(bitselector_10_out), .out(bitselector_20_out), .sel(3'b101));
  BitSelector bitselector_21 (.in(bitselector_10_out), .out(bitselector_21_out), .sel(3'b011));
  BitSelector bitselector_22 (.in(bitselector_10_out), .out(bitselector_22_out), .sel(3'b010));
  BitSelector bitselector_23 (.in(bitselector_10_out), .out(bitselector_23_out), .sel(3'b001));
  // DualRAM #(.addrWidth(16), .dataWidth(64), .enables("line"), .line("octo"), .misaligned("true"), .\type ("nonvolatile")) regY: pin names not known; wires that end beside it: bitselector_4_out, bitselector_3_out, regX_p2, regX_p2, bitselector_23_out, bitselector_22_out, bitselector_21_out, bitselector_19_out, bitselector_20_out, regY_p10, regY_p11, regY_p12, regY_p13, regY_p14, regY_p15, regY_p16, regY_p17
  Clock clock_4 (.out(clock_4_out));
  or or_2 (regX_p2, comparator_3_eq, and_2_out, alu_1_we);
  Multiplexer #(.select(4), .width(64)) multiplexer_2 (
    .in0(ram1_p10), .in1(ram1_p10), .in2({{32{1'b0}}, bitselector_4_out, bitselector_5_out}), .in3(undriven),
    .in4(alu_1_outx), .in5(alu_1_outx), .in6(alu_1_outx), .in7(alu_1_outx), .in8(alu_1_outx), .out(regX_p12),
    .sel(bitselector_12_out));  // open: in9, in10, in11, in12, in13, in14, in15
  BitSelector bitselector_24 (.in(bitselector_10_out), .out(bitselector_24_out), .sel(3'b111));
  BitSelector bitselector_25 (.in(bitselector_10_out), .out(bitselector_25_out), .sel(3'b110));
  BitSelector bitselector_26 (.in(bitselector_10_out), .out(bitselector_26_out), .sel(3'b101));
  BitSelector bitselector_27 (.in(bitselector_10_out), .out(bitselector_27_out), .sel(3'b100));
  BitSelector bitselector_28 (.in(bitselector_10_out), .out(bitselector_28_out), .sel(3'b011));
  BitSelector bitselector_29 (.in(bitselector_10_out), .out(bitselector_29_out), .sel(3'b010));
  BitSelector bitselector_30 (.in(bitselector_10_out), .out(bitselector_30_out), .sel(3'b001));
  Clock clock_5 (.out(clock_5_out));
  BitSelector #(.group(24), .width(64)) bitselector_31 (.in(regX_p13), .out(bitselector_31_out), .sel(2'b00));
  BitSelector #(.group(24), .width(64)) bitselector_32 (.in(regY_p10), .out(bitselector_32_out), .sel(2'b00));
  // DualRAM #(.addrWidth(16), .dataWidth(64), .enables("line"), .line("octo"), .misaligned("true"), .\type ("nonvolatile")) regZ: pin names not known; wires that end beside it: bitselector_5_out, bitselector_3_out, regX_p2, regX_p2, bitselector_30_out, bitselector_29_out, bitselector_28_out, bitselector_27_out, bitselector_26_out, regZ_p10, regZ_p11, regZ_p12, regZ_p13, regZ_p14, regZ_p15, regZ_p16, regZ_p17
  Counter #(.max('hffffff), .width(24)) counter_2 (
    .load(multiplexer_1_out), .D(bitselector_31_out), .count(not_3_out), .Q(counter_2_q), .clk(clock_6_out));  // open: carry, up, clr
  not not_3 (not_3_out, and_3_out);
  Clock clock_6 (.out(clock_6_out));
  // DualRAM #(.addrWidth(24), .dataWidth(64), .enables("line"), .line("octo"), .misaligned("true"), .\type ("nonvolatile")) ram1: pin names not known; wires that end beside it: counter_2_q, bitselector_32_out, and_1_out, and_1_out, 1'b0, 1'b0, 1'b0, 1'b0, 1'b0, ram1_p10
  Clock clock_7 ();  // open: out
endmodule

module alu (
  input  [63:0] argY,
  input  [63:0] argZ,
  input  [3:0] op,
  input  [3:0] \var ,
  output [63:0] outX,
  output we
);

  wire adder_1_cout, and_2_out, and_3_out, clock_1_out, clock_2_out, comparator_1_eq, comparator_2_eq,
       comparator_2_lt, comparator_3_eq, comparator_4_eq, comparator_5_eq, comparator_6_eq, comparator_7_eq,
       comparator_8_eq, fpclassificator_1_p1, fpclassificator_1_p2, fpcomparator_1_p3, fpcomparator_1_p4,
       multiplexer_1_out, not_2_out, subtractor_1_bout;
  wire [1:0] bitselector_2_out;
  wire [5:0] bitselector_1_out;
  wire [63:0] adder_1_out, and_1_out, bit_extender_1_out, bit_extender_2_out, bit_extender_3_out,
       bit_extender_4_out, buffer_1_out, counter_1_q, divider_1_out, divider_1_rem, fpadder_1_out,
       fpdivider_1_out, fpexponentiator_1_p1, fplogarithm_1_p3, fpmultiplier_1_out, fpnegator_1_p2,
       fpsquareroot_1_p1, fpsubtractor_1_out, fptoint_1_p1, fptoint_2_p1, fptoint_3_p1, fptoint_4_p1,
       fptrigonometry_1_p5, fptrigonometry_1_p6, fptrigonometry_1_p7, fptrigonometry_2_p2,
       fptrigonometry_2_p3, fptrigonometry_2_p4, inttofp_1_p1, multiplexer_2_out, multiplexer_3_out,
       multiplexer_4_out, multiplexer_5_out, multiplexer_6_out, multiplier_1_cout, multiplier_1_out,
       nand_1_out, negator_1_out, nor_1_out, not_1_out, or_1_out, shifter_1_out, shifter_2_out,
       shifter_3_out, shifter_4_out, shifter_5_out, subtractor_1_out, undriven, xnor_1_out, xor_1_out;

  BitSelector #(.group(6), .width(64)) bitselector_1 (.in(argZ), .out(bitselector_1_out), .sel(4'b0000));
  Comparator #(.mode("unsigned"), .width(4)) comparator_1 (.a(op), .b(4'b0100), .eq(comparator_1_eq));  // open: gt, lt
  BitSelector #(.group(2), .width(4)) bitselector_2 (.in(\var ), .out(bitselector_2_out), .sel(1'b0));
  Comparator #(.width(64)) comparator_2 (
    .a(argY), .b({64{1'b0}}), .eq(comparator_2_eq), .lt(comparator_2_lt));  // open: gt
  // FPComparator #(.fpwidth(64)) fpcomparator_1: pin names not known; wires that end beside it: argY, {64{1'b0}}, fpcomparator_1_p3, fpcomparator_1_p4
  Comparator #(.mode("unsigned"), .width(4)) comparator_3 (.a(op), .b(4'b0101), .eq(comparator_3_eq));  // open: gt, lt
  Adder #(.width(64)) adder_1 (.a(argZ), .b(argY), .out(adder_1_out), .cout(adder_1_cout));  // open: cin
  assign bit_extender_1_out = {{63{1'b0}}, adder_1_cout};  // Bit_Extender bit_extender_1
  Comparator #(.mode("unsigned"), .width(4)) comparator_4 (.a(op), .b(4'b0110), .eq(comparator_4_eq));  // open: gt, lt
  Shifter #(.width(64)) shifter_1 (.in(argY), .\dist (bitselector_1_out), .out(shifter_1_out));
  Comparator #(.mode("unsigned"), .width(4)) comparator_5 (.a(op), .b(4'b0111), .eq(comparator_5_eq));  // open: gt, lt
  FPAdder #(.fpwidth(64)) fpadder_1 (.a(argY), .b(argZ), .out(fpadder_1_out));
  Comparator #(.mode("unsigned"), .width(4)) comparator_6 (.a(op), .b(4'b1000), .eq(comparator_6_eq));  // open: gt, lt
  // FPTrigonometry #(.fpwidth(64)) fptrigonometry_1: pin names not known; wires that end beside it: \var , op, argY, argZ, fptrigonometry_1_p5, fptrigonometry_1_p6, fptrigonometry_1_p7
  Multiplexer #(.select(2)) multiplexer_1 (
    .in0(comparator_2_eq), .in1(comparator_2_lt), .in2(fpcomparator_1_p3), .in3(fpcomparator_1_p4),
    .out(multiplexer_1_out), .sel(bitselector_2_out));
  Multiplexer #(.select(4), .width(64)) multiplexer_2 (
    .in0(adder_1_out), .in1(bit_extender_1_out), .in2(subtractor_1_out), .in3(bit_extender_2_out),
    .in4(multiplier_1_out), .in5(multiplier_1_cout), .in6(divider_1_out), .in7(divider_1_rem),
    .in8(negator_1_out), .in9(counter_1_q), .in10(undriven), .out(multiplexer_2_out), .sel(\var ));  // open: in11, in12, in13, in14, in15
  Subtractor #(.width(64)) subtractor_1 (
    .a(argY), .b(argZ), .out(subtractor_1_out), .bout(subtractor_1_bout));  // open: bin
  Multiplexer #(.select(4), .width(64)) multiplexer_3 (
    .in0(shifter_1_out), .in1(shifter_2_out), .in2(shifter_3_out), .in3(shifter_4_out), .in4(shifter_5_out),
    .in5(buffer_1_out), .in6(not_1_out), .in7(or_1_out), .in8(and_1_out), .in9(nand_1_out), .in10(nor_1_out),
    .in11(xor_1_out), .in12(xnor_1_out), .out(multiplexer_3_out), .sel(\var ));  // open: in13, in14, in15
  Shifter #(.shift("lr"), .width(64)) shifter_2 (.in(argY), .\dist (bitselector_1_out), .out(shifter_2_out));
  Multiplexer #(.select(4), .width(64)) multiplexer_4 (
    .in0(fpadder_1_out), .in1(fpsubtractor_1_out), .in2(fpmultiplier_1_out), .in3(fpdivider_1_out),
    .in4(fpnegator_1_p2), .in5(inttofp_1_p1), .in6(fptoint_1_p1), .in7(fptoint_2_p1), .in8(fptoint_3_p1),
    .in9(fptoint_4_p1), .in10(bit_extender_3_out), .in11(bit_extender_4_out), .out(multiplexer_4_out),
    .sel(\var ));  // open: in12, in13, in14, in15
  FPSubtractor #(.fpwidth(64)) fpsubtractor_1 (.a(argY), .b(argZ), .out(fpsubtractor_1_out));
  Multiplexer #(.select(4), .width(64)) multiplexer_5 (
    .in0(fptrigonometry_1_p5), .in1(fptrigonometry_1_p6), .in2(fptrigonometry_1_p7),
    .in3(fptrigonometry_2_p2), .in4(fptrigonometry_2_p3), .in5(fptrigonometry_2_p4), .in6(fplogarithm_1_p3),
    .in7(fpexponentiator_1_p1), .in8(fpsquareroot_1_p1), .out(multiplexer_5_out), .sel(\var ));  // open: in9, in10, in11, in12, in13, in14, in15
  // FPTrigonometry #(.fpwidth(64), .\type ("arc")) fptrigonometry_2: pin names not known; wires that end beside it: argY, fptrigonometry_2_p2, fptrigonometry_2_p3, fptrigonometry_2_p4
  assign bit_extender_2_out = {{63{1'b0}}, subtractor_1_bout};  // Bit_Extender bit_extender_2
  Shifter #(.shift("ar"), .width(64)) shifter_3 (.in(argY), .\dist (bitselector_1_out), .out(shifter_3_out));
  FPMultiplier #(.fpwidth(64)) fpmultiplier_1 (.a(argY), .b(argZ), .out(fpmultiplier_1_out));
  // FPLogarithm #(.fpwidth(64)) fplogarithm_1: pin names not known; wires that end beside it: argY, argZ, fplogarithm_1_p3, argY, argZ
  Multiplexer #(.width(64)) multiplexer_6 (
    .in0({64{1'b0}}), .in1(64'h1), .out(multiplexer_6_out), .sel(multiplexer_1_out));
  Multiplier #(.width(64)) multiplier_1 (
    .a(argY), .b(argZ), .out(multiplier_1_out), .cout(multiplier_1_cout));  // open: cin
  Shifter #(.shift("rl"), .width(64)) shifter_4 (.in(argY), .\dist (bitselector_1_out), .out(shifter_4_out));
  FPDivider #(.fpwidth(64)) fpdivider_1 (.a(argY), .b(argZ), .out(fpdivider_1_out));
  // FPExponentiator #(.fpwidth(64)) fpexponentiator_1: pin names not known; wires that end beside it: fpexponentiator_1_p1, argY
  Divider #(.mode("twosComplement"), .width(64)) divider_1 (
    .a(argY), .b(argZ), .out(divider_1_out), .rem(divider_1_rem));  // open: upper
  assign not_1_out = ~argY;  // NOT_Gate not_1, 64 bits wide
  assign or_1_out = argY | argZ;  // OR_Gate or_1, 64 bits wide
  assign buffer_1_out = argY;  // Buffer buffer_1, 64 bits wide
  Shifter #(.shift("rr"), .width(64)) shifter_5 (.in(argY), .\dist (bitselector_1_out), .out(shifter_5_out));
  // FPNegator #(.fpwidth(64)) fpnegator_1: pin names not known; wires that end beside it: argY, fpnegator_1_p2, argY
  // IntToFP #(.fpwidth(64), .width(64)) inttofp_1: pin names not known; wires that end beside it: inttofp_1_p1, argY
  // FPSquareRoot #(.fpwidth(64)) fpsquareroot_1: pin names not known; wires that end beside it: fpsquareroot_1_p1
  Negator #(.width(64)) negator_1 (.in(argY), .out(negator_1_out));
  assign nand_1_out = ~(argY & argZ);  // NAND_Gate nand_1, 64 bits wide
  assign nor_1_out = ~(argY | argZ);  // NOR_Gate nor_1, 64 bits wide
  assign and_1_out = argY & argZ;  // AND_Gate and_1, 64 bits wide
  // FPToInt #(.fpwidth(64), .width(64)) fptoint_1: pin names not known; wires that end beside it: fptoint_1_p1, argY
  Comparator #(.mode("unsigned"), .width(4)) comparator_7 (
    .a(\var ), .b(4'b1001), .eq(comparator_7_eq));  // open: gt, lt
  and and_2 (and_2_out, comparator_7_eq, comparator_3_eq);
  not not_2 (not_2_out, comparator_8_eq);
  Comparator #(.width(64)) comparator_8 (.a({64{1'b0}}), .b(argY), .eq(comparator_8_eq));  // open: gt, lt
  assign xnor_1_out = ~(argY ^ argZ);  // XNOR_Gate xnor_1, 64 bits wide
  assign xor_1_out = argY ^ argZ;  // XOR_Gate xor_1, 64 bits wide
  // FPToInt #(.fpwidth(64), .mode("floor"), .width(64)) fptoint_2: pin names not known; wires that end beside it: fptoint_2_p1, argY
  and and_3 (and_3_out, and_2_out, not_2_out);
  Counter #(.max('hffffffffffffffff), .width(64)) counter_1 (
    .load(and_3_out), .D(argZ), .Q(counter_1_q), .clk(clock_1_out));  // open: count, carry, up, clr
  Clock clock_1 (.out(clock_1_out));
  // FPToInt #(.fpwidth(64), .mode("ceil"), .width(64)) fptoint_3: pin names not known; wires that end beside it: fptoint_3_p1, argY
  Random #(.seed(12345667), .width(64)) random_1 ();  // open: clk, next, out, clr
  Clock clock_2 (.out(clock_2_out));
  // FPToInt #(.fpwidth(64), .mode("truncate"), .width(64)) fptoint_4: pin names not known; wires that end beside it: fptoint_4_p1, argY
  // FPClassificator #(.fpwidth(64)) fpclassificator_1: pin names not known; wires that end beside it: fpclassificator_1_p1, fpclassificator_1_p2
  assign bit_extender_3_out = {{63{1'b0}}, fpclassificator_1_p1};  // Bit_Extender bit_extender_3
  assign bit_extender_4_out = {{63{1'b0}}, fpclassificator_1_p2};  // Bit_Extender bit_extender_4
  or or_2 (we, comparator_1_eq, comparator_3_eq, comparator_4_eq, comparator_5_eq, comparator_6_eq);
  Multiplexer #(.select(4), .width(64)) multiplexer_7 (
    .in4(multiplexer_6_out), .in5(multiplexer_2_out), .in6(multiplexer_3_out), .in7(multiplexer_4_out),
    .in8(multiplexer_5_out), .out(outX), .sel(op));  // open: in0, in1, in2, in3, in9, in10, in11, in12, in13, in14, in15
endmodule
